# Fritzing sketch blue (saved by Fritzing 0.9.4)
breadboards: 1

parts:
  Part1 = Arduino Uno (Rev3)
  R1 = Resistor [tolerance=±5% resistance=220 package=THT]
  LED1 = LED - 5mm [color="Red (633nm)" package="5 mm [THT]"]
  Part2 = Bluetooth HC-05 Macho  # not connected

nets:
  N1: Part1.D8, LED1.cathode
  N2: R1.Pin_0, LED1.anode
